# Fritzing sketch Sketch final proj (saved by Fritzing 0.9.4)
breadboards: 1

parts:
  J1 = Basic Servo
  Componente3 = Arduino Uno (Rev3) - ICSP  # not connected
  U3 = LCD-16X2 [package=lcd-16x2]
  R2 = Resistor [tolerance=±5% resistance=220 package=THT]
  Componente1 = Arduino Ethernet Shield (Rev3)
  R3 = Resistor [tolerance=±5% resistance=220 package=THT]
  R4 = Resistor [tolerance=±5% resistance=220 package=THT]
  LED1 = LED - 3mm [color="Red (633nm)" package="3 mm [THT]"]
  2_Channel_Relay1 = 2 Channel Power Relay
  부품5 = FC-28 Soil Hygrometer Module - Probe
  부품6 = FC-28 Soil Hygrometer Module

nets:
  GND: J1.gnd, U3.VSS, U3.R_W, U3.K, R2.Pin_1, Componente1.GND, R4.Pin_1, 2_Channel_Relay1.GND, 부품6.GND
  VCC: J1.vcc, U3.VDD, Componente1.5V, R3.Pin_1, 2_Channel_Relay1.VCC, 2_Channel_Relay1.K2-NO
  N1: J1.pulse, Componente1.PWM_D9
  N2: U3.VO, R2.Pin_0
  N3: U3.RS, Componente1.D2
  N4: U3.E, Componente1.PWM_D3
  N5: U3.DB4, Componente1.SDCS
  N6: U3.DB5, Componente1.PWM_D5
  N7: U3.DB6, Componente1.PWM_D6
  N8: U3.DB7, Componente1.D7
  N9: U3.A, R3.Pin_0
  N10: Componente1.A0, 부품6.VCC
  N11: Componente1.A3, 2_Channel_Relay1.IN2
  N12: Componente1.VIN, 부품6.AO
  N13: R4.Pin_0, LED1.cathode
  N14: LED1.anode, 2_Channel_Relay1.K2-COM
  N15: 부품5.POS, 부품6.POS
  N16: 부품5.NEG, 부품6.NEG

custom parts:
  2 Channel Power Relay: A 2 channel power relay. The module operates at 5V.
  FC-28 Soil Hygrometer Module - Probe: The FC-28 is a soil hygrometer module that uses the Texas Instruments LM393 comparator chip to provide an analog measurement of soil humidity.
  FC-28 Soil Hygrometer Module: The FC-28 is a soil hygrometer module that uses the Texas Instruments LM393 comparator chip to provide an analog measurement of soil humidity. The digital output is high when soil moisture is over a certain threshold, as determined by adjusting the potentiometer.
